// Logisim project WITCPU.circ as structural Verilog: 5 circuits, main circuit main
module main (
  input  [3:0] in_1,
  input  [3:0] in_2,
  input  [15:0] Rd,
  input  [3:0] in_4,
  output [15:0] Rx,
  output [15:0] Ry
);

  wire clock_1_out, demultiplexer_1_out0, demultiplexer_1_out1, demultiplexer_1_out2, demultiplexer_1_out3,
       demultiplexer_1_out4, demultiplexer_1_out5, demultiplexer_1_out6, demultiplexer_1_out7,
       demultiplexer_1_out8, demultiplexer_1_out9, demultiplexer_1_out10, demultiplexer_1_out11,
       demultiplexer_1_out12, demultiplexer_1_out13, demultiplexer_1_out14, demultiplexer_1_out15;
  wire [15:0] R0_q, R1_q, R2_q, R3_q, R4_q, R5_q, R6_q, R7_q, R8_q, R9_q, Ra_q, Rb_q, Rc_q, Rd_q, Re_q, Rf_q;

  Clock clock_1 (.out(clock_1_out));
  Demultiplexer #(.select(4)) demultiplexer_1 (
    .out0(demultiplexer_1_out0), .out1(demultiplexer_1_out1), .out2(demultiplexer_1_out2),
    .out3(demultiplexer_1_out3), .out4(demultiplexer_1_out4), .out5(demultiplexer_1_out5),
    .out6(demultiplexer_1_out6), .out7(demultiplexer_1_out7), .out8(demultiplexer_1_out8),
    .out9(demultiplexer_1_out9), .out10(demultiplexer_1_out10), .out11(demultiplexer_1_out11),
    .out12(demultiplexer_1_out12), .out13(demultiplexer_1_out13), .out14(demultiplexer_1_out14),
    .out15(demultiplexer_1_out15), .in(clock_1_out), .sel(in_2));  // open: en
  Register #(.width(16)) R0 (.D(Rd), .Q(R0_q), .clk(demultiplexer_1_out0));  // open: en, clr
  Register #(.width(16)) R2 (.D(Rd), .Q(R2_q), .clk(demultiplexer_1_out2));  // open: en, clr
  Register #(.width(16)) R1 (.D(Rd), .Q(R1_q), .clk(demultiplexer_1_out1));  // open: en, clr
  Register #(.width(16)) R4 (.D(Rd), .Q(R4_q));  // open: en, clk, clr
  Register #(.width(16)) R3 (.D(Rd), .Q(R3_q), .clk(demultiplexer_1_out3));  // open: en, clr
  Register #(.width(16)) R5 (.D(Rd), .Q(R5_q), .clk(demultiplexer_1_out5));  // open: en, clr
  Register #(.width(16)) R6 (.D(Rd), .Q(R6_q));  // open: en, clk, clr
  Register #(.width(16)) R7 (.D(Rd), .Q(R7_q), .clk(demultiplexer_1_out7));  // open: en, clr
  Register #(.width(16)) R8 (.D(Rd), .Q(R8_q));  // open: en, clk, clr
  Register #(.width(16)) R9 (.D(Rd), .Q(R9_q), .clk(demultiplexer_1_out9));  // open: en, clr
  Register #(.width(16)) Ra (.D(Rd), .Q(Ra_q), .clk(demultiplexer_1_out10));  // open: en, clr
  Register #(.width(16)) Rb (.D(Rd), .Q(Rb_q), .clk(demultiplexer_1_out11));  // open: en, clr
  Register #(.width(16)) Rc (.D(Rd), .Q(Rc_q));  // open: en, clk, clr
  Register #(.width(16)) u_Rd (.D(Rd), .Q(Rd_q), .clk(demultiplexer_1_out13));  // open: en, clr
  Register #(.width(16)) Re (.D(Rd), .Q(Re_q), .clk(demultiplexer_1_out14));  // open: en, clr
  Register #(.width(16)) Rf (.D(Rd), .Q(Rf_q), .clk(demultiplexer_1_out15));  // open: en, clr
  Multiplexer #(.select(4), .width(16)) multiplexer_1 (
    .in0(R0_q), .in1(R1_q), .in2(R2_q), .in3(R3_q), .in4(R4_q), .in5(R5_q), .in6(R6_q), .in7(R7_q),
    .in8(R8_q), .in9(R9_q), .in10(Ra_q), .in11(Rb_q), .in12(Rc_q), .in13(Rd_q), .in14(Re_q), .in15(Rf_q),
    .out(Rx), .sel(in_1));  // open: en
  Multiplexer #(.select(4), .width(16)) multiplexer_2 (
    .in0(R0_q), .in1(R1_q), .in2(R2_q), .in3(R3_q), .in4(R4_q), .in5(R5_q), .in6(R6_q), .in7(R7_q),
    .in8(R8_q), .in9(R9_q), .in10(Ra_q), .in11(Rb_q), .in12(Rc_q), .in13(Rd_q), .in14(Re_q), .in15(Rf_q),
    .out(Ry), .sel(in_4));  // open: en
endmodule

module WITCPU (
);

  main main_1 ();  // open: in_2, Rd, Rx, in_1, Ry, in_4
endmodule

module ALU (
  input  in_1,
  input  [15:0] in_2,
  output [15:0] X,
  output [15:0] Y,
  output [3:0] out_5
);
endmodule

module PC_Controller (
  input  [7:0] Input,
  input  [7:0] PC_input,
  input  in_3,
  input  [15:0] Rx,
  input  in_5,
  input  [3:0] Opcode,
  output [7:0] Output
);

  wire clock_1_out;
  wire [7:0] adder_1_out, multiplexer_1_out;

  Multiplexer #(.width(8)) multiplexer_1 (
    .in0(PC_input), .in1(adder_1_out), .out(multiplexer_1_out), .sel(in_3));  // open: en
  Register register_1 (.D(multiplexer_1_out), .Q(Output), .clk(clock_1_out), .clr(in_5));  // open: en
  Clock clock_1 (.out(clock_1_out));
  Adder adder_1 (.a(Output), .b(Input), .out(adder_1_out));  // open: cin, cout
endmodule

module RAM (
  input  [7:0] Adress,
  input  [15:0] In,
  input  in_3,
  input  in_4,
  output [15:0] Out
);

  wire clock_1_out, not_1_out;

  not not_1 (not_1_out, in_4);
  Clock clock_1 (.out(clock_1_out));
  RAM_part #(.dataWidth(16), .bus("separate")) ram_1 (
    .addr(Adress), .din(In), .data(Out), .str(not_1_out), .sel(1'b1), .clk(clock_1_out), .ld(in_4), .clr(in_3));
endmodule
